# Fritzing sketch diagrama analógico (saved by Fritzing 0.8.7b)
breadboards: 1

parts:
  Parte1 = Arduino Mega 2560 (Rev3)
  M1 = DC Motor
  IC1 = L293D [package=THT]
  VCC1 = Battery

nets:
  N1: Parte1.GND, IC1.0V, VCC1.-
  N2: Parte1.D11_PWM, IC1.In_3
  N3: Parte1.D10_PWM, IC1.In_1
  N4: Parte1.D9_PWM, IC1.Enable_2
  N5: Parte1.5V, IC1.+Vmotor
  N6: M1.pin_1, IC1.Out_4_(_Controlled_by_Enable_2_)
  N7: M1.pin_2, IC1.Out_3_(_Controlled_by_Enable_2_)
  N8: IC1.+V, VCC1.+
