# Fritzing sketch diagrama digital de entrada (saved by Fritzing 0.8.7b)
breadboards: 1

parts:
  LED1 = LED - 5mm [color="Green (570nm)" package="5 mm [THT]"]
  LED2 = LED - 5mm [color="Yellow (595nm)" package="5 mm [THT]"]
  LED3 = LED - 5mm [color="Red (633nm)" package="5 mm [THT]"]
  Parte1 = Arduino Mega 2560 (Rev3)
  Display1 = LCD screen 16x2 IIC [part_number=101290]
  S1 = Pushbutton [package="[THT]"]
  R1 = Resistor [tolerance=±5% resistance=220 package=THT]
  R2 = Resistor [tolerance=±5% resistance=220 package=THT]
  R3 = Resistor [tolerance=±5% resistance=220 package=THT]
  R4 = Resistor [tolerance=±5% resistance=220 package=THT]

nets:
  N1: LED1.cathode, R2.Pin_1
  N2: LED1.anode, Parte1.D4_PWM
  N3: LED2.cathode, R3.Pin_1
  N4: LED3.cathode, R4.Pin_1
  N5: LED3.anode, Parte1.D2_PWM
  N6: Parte1.D21/SCL, Display1.SCL
  N7: Parte1.D20/SDA, Display1.SDA
  GND: Parte1.GND, Display1.GND, S1.Pin_1, S1.Pin_2, R1.Pin_0, R2.Pin_0, R3.Pin_0, R4.Pin_0
  N8: Parte1.D10_PWM, S1.Pin_3, S1.Pin_4, R1.Pin_1
  5V: Parte1.5V, Display1.VCC

custom parts:
  LCD screen 16x2 IIC: LCD screen with HD44780 controller enables showing text, symbols, value or anything else that comes from Croduino/Arduino. It is capable of showing 16 symbols in two lines and therefore can be used in many projects that need to send clearly visible and legible output information.. • Color of symbols: White • Backlight: Blue • Dimensions: 80 x 36 x 12 mm • Screen dimensions: 64.5 x 16 mm •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
